// Logisim project cpu.circ as structural Verilog: 12 circuits, main circuit main
module main (
  input  reset
);

  wire ALUinB, and_1_out, and_2_out, and_3_out, beq, bge, clk, DMwe, gt, inn, j, jal, jr, keyboard_1_avail,
       memory_latch_1_oe_latched, memory_latch_1_we_latched, not_1_out, or_1_out, or_2_out, or_3_out,
       or_4_out, outt, Rdst, Rwd, Rwe, shft, zero;
  wire [2:0] ALUop, multiplexer_1_out, multiplexer_3_out, multiplexer_4_out, rd, rs, rt, shamt;
  wire [5:0] immed;
  wire [6:0] keyboard_1_data;
  wire [11:0] addr;
  wire [15:0] alu_3_alu_out, ALU_out, bit_extender_1_out, bit_extender_2_out, bit_extender_3_out, in_val,
       lshift_1_dataout, lshift_2_dataout, memory_latch_1_address_latched, memory_latch_1_data_in_latched,
       multiplexer_2_out, multiplexer_5_out, multiplexer_6_out, multiplexer_7_out, multiplexer_9_out,
       multiplexer_10_out, multiplexer_11_out, multiplexer_12_out, pc_reg_1_dataout, PCInc, PCNext, RAM_out,
       rom_1_data, rs_out, rt_out;

  Clock u_clk (.out(clk));
  and and_1 (and_1_out, Rwe, clk);
  Multiplexer #(.width(3), .enable("false")) multiplexer_1 (.in0(rt), .in1(3'b111), .out(multiplexer_1_out), .sel(jal));
  Multiplexer #(.width(16), .enable("false")) multiplexer_2 (
    .in0(ALU_out), .in1(RAM_out), .out(multiplexer_2_out), .sel(Rwd));
  Multiplexer #(.width(3), .enable("false")) multiplexer_3 (
    .in0(rd), .in1(multiplexer_1_out), .out(multiplexer_3_out), .sel(Rdst));
  Multiplexer #(.width(3), .enable("false")) multiplexer_4 (
    .in0(rs), .in1(3'b000), .out(multiplexer_4_out), .sel(or_1_out));
  or or_1 (or_1_out, jal, inn);
  pc_reg pc_reg_1 (.dataIn(PCNext), .reset(reset), .clk(clk), .dataOut(pc_reg_1_dataout));
  ROM #(.addrWidth(16), .dataWidth(16)) rom_1 (.addr(pc_reg_1_dataout), .data(rom_1_data));
  ALU alu_1 (.data1(pc_reg_1_dataout), .ALUop(3'b000), .ALU_out(PCInc), .data2(16'h1));  // open: zero, gt
  // Probe on rt_out
  RegisterFile registerfile_1 (
    .dataIn(multiplexer_2_out), .reset(reset), .WE(and_1_out), .rd(multiplexer_3_out),
    .rt(multiplexer_1_out), .rs(multiplexer_4_out), .readdataRt(rt_out), .readdataRs(rs_out));
  // Probe on rs_out
  Keyboard #(.trigger("falling")) keyboard_1 (
    .clk(clk), .re(inn), .clr(reset), .avail(keyboard_1_avail), .data(keyboard_1_data));
  control control_1 (
    .insn(rom_1_data), .rs(rs), .rt(rt), .rd(rd), .shamt(shamt), .immed(immed), .addr(addr), .Rwe(Rwe),
    .DMwe(DMwe), .Rdst(Rdst), .Rwd(Rwd), .ALUop(ALUop), .ALUinB(ALUinB), .beq(beq), .bge(bge), .j(j),
    .jr(jr), .jal(jal), .in_8060aaad(inn), .out_b538a2af(outt), .shft(shft));
  assign bit_extender_1_out = {{10{immed[5]}}, immed};  // Bit_Extender bit_extender_1
  Multiplexer #(.width(16), .enable("false")) multiplexer_5 (
    .in0(bit_extender_1_out), .in1(PCInc), .out(multiplexer_5_out), .sel(jal));
  Multiplexer #(.width(16), .enable("false")) multiplexer_6 (
    .in0(multiplexer_5_out), .in1(in_val), .out(multiplexer_6_out), .sel(inn));
  Multiplexer #(.width(16), .enable("false")) multiplexer_7 (
    .in0(multiplexer_6_out), .in1(bit_extender_2_out), .out(multiplexer_7_out), .sel(shft));
  assign bit_extender_2_out = {{13{shamt[2]}}, shamt};  // Bit_Extender bit_extender_2
  Multiplexer #(.width(16), .enable("false")) multiplexer_8 (
    .in0(16'h80), .in1({{9{1'b0}}, keyboard_1_data}), .out(in_val), .sel(keyboard_1_avail));
  Multiplexer #(.width(16), .enable("false")) multiplexer_9 (
    .in0(multiplexer_7_out), .in1({16{1'b0}}), .out(multiplexer_9_out), .sel(jr));
  Multiplexer #(.width(16), .enable("false")) multiplexer_10 (
    .in0(rt_out), .in1(multiplexer_9_out), .out(multiplexer_10_out), .sel(ALUinB));
  not not_1 (not_1_out, clk);
  LShift lshift_1 (.dataOut(lshift_1_dataout), .shft({16{1'b0}}), .dataIn(multiplexer_9_out));
  // Probe on ALU_out
  ALU alu_2 (.data1(rs_out), .ALUop(ALUop), .ALU_out(ALU_out), .data2(multiplexer_10_out), .zero(zero), .gt(gt));
  TTY #(.rows(13), .cols(80)) tty_1 (.data(rs_out[6:0]), .clk(clk), .we(outt), .clr(reset));
  ALU alu_3 (.data1(lshift_1_dataout), .ALUop(3'b000), .ALU_out(alu_3_alu_out), .data2(PCInc));  // open: zero, gt
  and and_2 (and_2_out, zero, or_2_out);
  or or_2 (or_2_out, beq, bge);
  memory_latch memory_latch_1 (
    .address(ALU_out), .WE(DMwe), .clk(not_1_out), .data_in(rt_out),
    .address_latched(memory_latch_1_address_latched), .WE_latched(memory_latch_1_we_latched),
    .OE_latched(memory_latch_1_oe_latched), .data_in_latched(memory_latch_1_data_in_latched));
  Multiplexer #(.width(16), .enable("false")) multiplexer_11 (
    .in0(PCInc), .in1(alu_3_alu_out), .out(multiplexer_11_out), .sel(or_3_out));
  or or_3 (or_3_out, and_2_out, and_3_out);
  and and_3 (and_3_out, gt, bge);
  RAM #(.addrWidth(16), .dataWidth(16), .trigger("high"), .databus("bibus")) ram_1 (
    .addr(memory_latch_1_address_latched), .we(memory_latch_1_we_latched), .oe(memory_latch_1_oe_latched),
    .din(memory_latch_1_data_in_latched), .dout(RAM_out));
  assign bit_extender_3_out = {{4{addr[11]}}, addr};  // Bit_Extender bit_extender_3
  Multiplexer #(.width(16), .enable("false")) multiplexer_12 (
    .in0(multiplexer_11_out), .in1(lshift_2_dataout), .out(multiplexer_12_out), .sel(or_4_out));
  LShift lshift_2 (.dataOut(lshift_2_dataout), .shft({16{1'b0}}), .dataIn(bit_extender_3_out));
  or or_4 (or_4_out, jal, j);
  Multiplexer #(.width(16), .enable("false")) multiplexer_13 (
    .in0(multiplexer_12_out), .in1(rs_out), .out(PCNext), .sel(jr));

  // Notes on the sheet:
  //   contents of rom_1 (hex, n*v repeats v):
  //   2401
endmodule

module reg_16 (
  input  [15:0] dataIn,
  input  reset,
  input  clk,
  output [15:0] dataOut
);

  D_Flip_Flop d_ff_1 (.D(dataIn[0]), .clk(clk), .Q(dataOut[0]), .reset(reset));  // open: Qn, preset
  D_Flip_Flop d_ff_2 (.D(dataIn[1]), .clk(clk), .Q(dataOut[1]), .reset(reset));  // open: Qn, preset
  D_Flip_Flop d_ff_3 (.D(dataIn[2]), .clk(clk), .Q(dataOut[2]), .reset(reset));  // open: Qn, preset
  D_Flip_Flop d_ff_4 (.D(dataIn[3]), .clk(clk), .Q(dataOut[3]), .reset(reset));  // open: Qn, preset
  D_Flip_Flop d_ff_5 (.D(dataIn[4]), .clk(clk), .Q(dataOut[4]), .reset(reset));  // open: Qn, preset
  D_Flip_Flop d_ff_6 (.D(dataIn[5]), .clk(clk), .Q(dataOut[5]), .reset(reset));  // open: Qn, preset
  D_Flip_Flop d_ff_7 (.D(dataIn[6]), .clk(clk), .Q(dataOut[6]), .reset(reset));  // open: Qn, preset
  D_Flip_Flop d_ff_8 (.D(dataIn[7]), .clk(clk), .Q(dataOut[7]), .reset(reset));  // open: Qn, preset
  D_Flip_Flop d_ff_9 (.D(dataIn[8]), .clk(clk), .Q(dataOut[8]), .reset(reset));  // open: Qn, preset
  D_Flip_Flop d_ff_10 (.D(dataIn[9]), .clk(clk), .Q(dataOut[9]), .reset(reset));  // open: Qn, preset
  D_Flip_Flop d_ff_11 (.D(dataIn[10]), .clk(clk), .Q(dataOut[10]), .reset(reset));  // open: Qn, preset
  D_Flip_Flop d_ff_12 (.D(dataIn[11]), .clk(clk), .Q(dataOut[11]), .reset(reset));  // open: Qn, preset
  D_Flip_Flop d_ff_13 (.D(dataIn[12]), .clk(clk), .Q(dataOut[12]), .reset(reset));  // open: Qn, preset
  D_Flip_Flop d_ff_14 (.D(dataIn[13]), .clk(clk), .Q(dataOut[13]), .reset(reset));  // open: Qn, preset
  D_Flip_Flop d_ff_15 (.D(dataIn[14]), .clk(clk), .Q(dataOut[14]), .reset(reset));  // open: Qn, preset
  D_Flip_Flop d_ff_16 (.D(dataIn[15]), .clk(clk), .Q(dataOut[15]), .reset(reset));  // open: Qn, preset

  // Other names for the same wires on the sheet: in2[7:0] = dataIn[15:8]; out1[7:0] = dataOut[7:0]
endmodule

module ALU (
  input  [2:0] ALUop,
  input  [15:0] data1,
  input  [15:0] data2,
  output zero,
  output [15:0] ALU_out,
  output gt
);

  wire and_1_out;
  wire [15:0] add_out, lshft_out, nand_out, nor_out, rshft_out, sub_out;

  assign nor_out = ~(data1 | data2);  // NOR_Gate nor_1, 16 bits wide
  assign nand_out = ~(data1 & data2);  // NAND_Gate nand_1, 16 bits wide
  adder_16 adder_16_1 (.A(data1), .B(data2), .sub(1'b0), .result(add_out));  // open: ovf
  adder_16 adder_16_2 (.A(data1), .B(data2), .sub(1'b1), .result(sub_out));  // open: ovf
  Multiplexer #(.select(3), .width(16), .enable("false")) multiplexer_1 (
    .in0(add_out), .in1(sub_out), .in2(nor_out), .in3(nand_out), .in4(lshft_out), .in5(rshft_out),
    .out(ALU_out), .sel(ALUop));  // open: in6, in7
  LShift lshift_1 (.dataOut(lshft_out), .shft(data2), .dataIn(data1));
  RShift rshift_1 (.dataOut(rshft_out), .dataIn(data1), .shft(data2));
  and and_1 (and_1_out, sub_out[15], 1'b1);
  not not_1 (gt, and_1_out);
  nor nor_2 (zero, sub_out[0], sub_out[1], sub_out[2], sub_out[3], sub_out[4], sub_out[5], sub_out[6], sub_out[7], sub_out[8], sub_out[9], sub_out[10], sub_out[11], sub_out[12], sub_out[13], sub_out[14], sub_out[15]);

  // Other names for the same wires on the sheet: data_1[15:0] = data1; data_2[15:0] = data2
endmodule

module full_adder (
  input  Cin,
  input  A,
  input  B,
  output sum,
  output Cout
);

  wire and_1_out, and_2_out, xor_1_out;

  and and_1 (and_1_out, B, A);
  xor xor_1 (xor_1_out, A, B);
  or or_1 (Cout, and_1_out, and_2_out);
  and and_2 (and_2_out, xor_1_out, Cin);
  xor xor_2 (sum, Cin, xor_1_out);
endmodule

module adder_16 (
  input  [15:0] A,
  input  [15:0] B,
  input  sub,
  output [15:0] result,
  output ovf
);

  wire full_adder_1_cout, full_adder_2_cout, full_adder_3_cout, full_adder_4_cout, full_adder_5_cout,
       full_adder_6_cout, full_adder_7_cout, full_adder_8_cout, full_adder_9_cout, full_adder_10_cout,
       full_adder_11_cout, full_adder_12_cout, full_adder_13_cout, full_adder_14_cout, full_adder_15_cout,
       full_adder_16_cout, xor_1_out, xor_2_out, xor_3_out, xor_4_out, xor_5_out, xor_6_out, xor_7_out,
       xor_8_out, xor_9_out, xor_10_out, xor_11_out, xor_12_out, xor_13_out, xor_14_out, xor_15_out,
       xor_16_out;

  // Probe on result
  xor xor_1 (xor_1_out, sub, B[0]);
  xor xor_2 (xor_2_out, sub, B[1]);
  xor xor_3 (xor_3_out, sub, B[2]);
  xor xor_4 (xor_4_out, sub, B[3]);
  xor xor_5 (xor_5_out, sub, B[4]);
  xor xor_6 (xor_6_out, sub, B[5]);
  xor xor_7 (xor_7_out, sub, B[6]);
  xor xor_8 (xor_8_out, sub, B[7]);
  full_adder full_adder_1 (.Cout(full_adder_1_cout), .A(A[0]), .B(xor_1_out), .Cin(sub), .sum(result[0]));
  full_adder full_adder_2 (.Cout(full_adder_2_cout), .A(A[1]), .B(xor_2_out), .Cin(full_adder_1_cout), .sum(result[1]));
  full_adder full_adder_3 (.Cout(full_adder_3_cout), .A(A[2]), .B(xor_3_out), .Cin(full_adder_2_cout), .sum(result[2]));
  full_adder full_adder_4 (.Cout(full_adder_4_cout), .A(A[3]), .B(xor_4_out), .Cin(full_adder_3_cout), .sum(result[3]));
  full_adder full_adder_5 (.Cout(full_adder_5_cout), .A(A[4]), .B(xor_5_out), .Cin(full_adder_4_cout), .sum(result[4]));
  full_adder full_adder_6 (.Cout(full_adder_6_cout), .A(A[5]), .B(xor_6_out), .Cin(full_adder_5_cout), .sum(result[5]));
  full_adder full_adder_7 (.Cout(full_adder_7_cout), .A(A[6]), .B(xor_7_out), .Cin(full_adder_6_cout), .sum(result[6]));
  full_adder full_adder_8 (.Cout(full_adder_8_cout), .A(A[7]), .B(xor_8_out), .Cin(full_adder_7_cout), .sum(result[7]));
  full_adder full_adder_9 (
    .Cout(full_adder_9_cout), .A(A[15]), .B(xor_9_out), .Cin(full_adder_10_cout), .sum(result[15]));
  full_adder full_adder_10 (
    .Cout(full_adder_10_cout), .A(A[14]), .B(xor_10_out), .Cin(full_adder_11_cout), .sum(result[14]));
  full_adder full_adder_11 (
    .Cout(full_adder_11_cout), .A(A[13]), .B(xor_11_out), .Cin(full_adder_12_cout), .sum(result[13]));
  full_adder full_adder_12 (
    .Cout(full_adder_12_cout), .A(A[12]), .B(xor_12_out), .Cin(full_adder_13_cout), .sum(result[12]));
  full_adder full_adder_13 (
    .Cout(full_adder_13_cout), .A(A[11]), .B(xor_13_out), .Cin(full_adder_14_cout), .sum(result[11]));
  full_adder full_adder_14 (
    .Cout(full_adder_14_cout), .A(A[10]), .B(xor_14_out), .Cin(full_adder_15_cout), .sum(result[10]));
  full_adder full_adder_15 (
    .Cout(full_adder_15_cout), .A(A[9]), .B(xor_15_out), .Cin(full_adder_16_cout), .sum(result[9]));
  full_adder full_adder_16 (
    .Cout(full_adder_16_cout), .A(A[8]), .B(xor_16_out), .Cin(full_adder_8_cout), .sum(result[8]));
  xor xor_9 (xor_9_out, B[15], sub);
  xor xor_10 (xor_10_out, B[14], sub);
  xor xor_11 (xor_11_out, B[13], sub);
  xor xor_12 (xor_12_out, B[12], sub);
  xor xor_13 (xor_13_out, B[11], sub);
  xor xor_14 (xor_14_out, B[10], sub);
  xor xor_15 (xor_15_out, B[9], sub);
  xor xor_16 (xor_16_out, B[8], sub);
  xor xor_17 (ovf, full_adder_9_cout, full_adder_10_cout);

  // Other names for the same wires on the sheet: A7[7:0] = A[7:0]; A16[7:0] = A[15:8]; B7[7:0] = B[7:0];
  //   B16[7:0] = B[15:8]
endmodule

module RegisterFile (
  input  [15:0] dataIn,
  input  reset,
  input  WE,
  input  [2:0] rd,
  input  [2:0] rt,
  input  [2:0] rs,
  output [15:0] readdataRt,
  output [15:0] readdataRs
);

  wire and_1_out, and_2_out, and_3_out, and_4_out, and_5_out, and_6_out, and_7_out, and_8_out, d1_0, d1_1,
       d1_2, d1_3, d1_4, d1_5, d1_6, d1_7, d2_0, d2_1, d2_2, d2_3, d2_4, d2_5, d2_6, d2_7, decoder_1_out0,
       decoder_1_out1, decoder_1_out2, decoder_1_out3, decoder_1_out4, decoder_1_out5, decoder_1_out6,
       decoder_1_out7;
  wire [15:0] reg_16_1_dataout, reg_16_2_dataout, reg_16_3_dataout, reg_16_4_dataout, reg_16_5_dataout,
       reg_16_6_dataout, reg_16_7_dataout, reg_16_8_dataout;

  Decoder #(.select(3), .enable("false")) decoder_1 (
    .out0(decoder_1_out0), .out1(decoder_1_out1), .out2(decoder_1_out2), .out3(decoder_1_out3),
    .out4(decoder_1_out4), .out5(decoder_1_out5), .out6(decoder_1_out6), .out7(decoder_1_out7), .sel(rd));
  Decoder #(.select(3), .enable("false")) decoder_2 (
    .out0(d1_0), .out1(d1_1), .out2(d1_2), .out3(d1_3), .out4(d1_4), .out5(d1_5), .out6(d1_6), .out7(d1_7),
    .sel(rt));
  and and_1 (and_1_out, 1'b0, decoder_1_out0);
  and and_2 (and_2_out, WE, decoder_1_out1);
  and and_3 (and_3_out, WE, decoder_1_out2);
  and and_4 (and_4_out, WE, decoder_1_out3);
  and and_5 (and_5_out, WE, decoder_1_out4);
  and and_6 (and_6_out, WE, decoder_1_out5);
  and and_7 (and_7_out, WE, decoder_1_out6);
  and and_8 (and_8_out, WE, decoder_1_out7);
  Decoder #(.select(3), .enable("false")) decoder_3 (
    .out0(d2_0), .out1(d2_1), .out2(d2_2), .out3(d2_3), .out4(d2_4), .out5(d2_5), .out6(d2_6), .out7(d2_7),
    .sel(rs));
  // Probe on reg_16_1_dataout
  reg_16 reg_16_1 (.dataIn(dataIn), .reset(reset), .clk(and_1_out), .dataOut(reg_16_1_dataout));
  // Probe on reg_16_2_dataout
  reg_16 reg_16_2 (.dataIn(dataIn), .reset(reset), .clk(and_2_out), .dataOut(reg_16_2_dataout));
  // Probe on reg_16_3_dataout
  reg_16 reg_16_3 (.dataIn(dataIn), .reset(reset), .clk(and_3_out), .dataOut(reg_16_3_dataout));
  // Probe on reg_16_4_dataout
  reg_16 reg_16_4 (.dataIn(dataIn), .reset(reset), .clk(and_4_out), .dataOut(reg_16_4_dataout));
  // Probe on reg_16_5_dataout
  reg_16 reg_16_5 (.dataIn(dataIn), .reset(reset), .clk(and_5_out), .dataOut(reg_16_5_dataout));
  // Probe on reg_16_6_dataout
  reg_16 reg_16_6 (.dataIn(dataIn), .reset(reset), .clk(and_6_out), .dataOut(reg_16_6_dataout));
  // Probe on reg_16_7_dataout
  reg_16 reg_16_7 (.dataIn(dataIn), .reset(reset), .clk(and_7_out), .dataOut(reg_16_7_dataout));
  // Probe on reg_16_8_dataout
  reg_16 reg_16_8 (.dataIn(dataIn), .reset(reset), .clk(and_8_out), .dataOut(reg_16_8_dataout));
  assign readdataRt = d1_0 ? reg_16_1_dataout : 16'bz;  // Controlled_Buffer controlled_buffer_1
  assign readdataRs = d2_0 ? reg_16_1_dataout : 16'bz;  // Controlled_Buffer controlled_buffer_2
  assign readdataRt = d1_1 ? reg_16_2_dataout : 16'bz;  // Controlled_Buffer controlled_buffer_3
  assign readdataRs = d2_1 ? reg_16_2_dataout : 16'bz;  // Controlled_Buffer controlled_buffer_4
  assign readdataRt = d1_2 ? reg_16_3_dataout : 16'bz;  // Controlled_Buffer controlled_buffer_5
  assign readdataRs = d2_2 ? reg_16_3_dataout : 16'bz;  // Controlled_Buffer controlled_buffer_6
  assign readdataRt = d1_3 ? reg_16_4_dataout : 16'bz;  // Controlled_Buffer controlled_buffer_7
  assign readdataRs = d2_3 ? reg_16_4_dataout : 16'bz;  // Controlled_Buffer controlled_buffer_8
  assign readdataRt = d1_4 ? reg_16_5_dataout : 16'bz;  // Controlled_Buffer controlled_buffer_9
  assign readdataRs = d2_4 ? reg_16_5_dataout : 16'bz;  // Controlled_Buffer controlled_buffer_10
  assign readdataRt = d1_5 ? reg_16_6_dataout : 16'bz;  // Controlled_Buffer controlled_buffer_11
  assign readdataRs = d2_5 ? reg_16_6_dataout : 16'bz;  // Controlled_Buffer controlled_buffer_12
  assign readdataRt = d1_6 ? reg_16_7_dataout : 16'bz;  // Controlled_Buffer controlled_buffer_13
  assign readdataRs = d2_6 ? reg_16_7_dataout : 16'bz;  // Controlled_Buffer controlled_buffer_14
  assign readdataRt = d1_7 ? reg_16_8_dataout : 16'bz;  // Controlled_Buffer controlled_buffer_15
  assign readdataRs = d2_7 ? reg_16_8_dataout : 16'bz;  // Controlled_Buffer controlled_buffer_16

  // Other names for the same wires on the sheet: DIn[15:0] = dataIn; res = reset
endmodule

module memory_latch (
  input  [15:0] address,
  input  WE,
  input  clk,
  input  [15:0] data_in,
  output [15:0] address_latched,
  output WE_latched,
  output OE_latched,
  output [15:0] data_in_latched
);

  wire DMwe_latch_q;
  wire [15:0] addr_latch_q;

  Register #(.width(16), .trigger("falling")) addr_latch (
    .D(address), .en(WE), .clk(clk), .Q(addr_latch_q));  // open: clr
  D_Flip_Flop #(.trigger("falling")) DMwe_latch (.D(WE), .clk(clk), .Q(DMwe_latch_q));  // open: Qn, preset, reset
  Register #(.width(16), .trigger("falling")) data_to_be_written (
    .D(data_in), .en(WE), .clk(clk), .Q(data_in_latched));  // open: clr
  Multiplexer #(.width(16), .enable("false")) multiplexer_1 (
    .in0(address), .in1(addr_latch_q), .out(address_latched), .sel(DMwe_latch_q));
  and and_1 (WE_latched, clk, DMwe_latch_q);
  not not_1 (OE_latched, WE_latched);
endmodule

module LShift (
  input  [15:0] shft,
  input  [15:0] dataIn,
  output [15:0] dataOut
);

  wire multiplexer_1_out, multiplexer_2_out, multiplexer_3_out, multiplexer_4_out, multiplexer_5_out,
       multiplexer_6_out, multiplexer_7_out, multiplexer_8_out, multiplexer_9_out, multiplexer_10_out,
       multiplexer_11_out, multiplexer_12_out, multiplexer_13_out, multiplexer_14_out, multiplexer_15_out,
       multiplexer_16_out, multiplexer_17_out, multiplexer_18_out, multiplexer_19_out, multiplexer_20_out,
       multiplexer_21_out, multiplexer_22_out, multiplexer_23_out, multiplexer_24_out, multiplexer_25_out,
       multiplexer_26_out, multiplexer_27_out, multiplexer_28_out, multiplexer_29_out, multiplexer_30_out,
       multiplexer_31_out, multiplexer_32_out;

  Multiplexer #(.enable("false")) multiplexer_1 (
    .in0(dataIn[15]), .in1(dataIn[11]), .out(multiplexer_1_out), .sel(shft[2]));
  Multiplexer #(.enable("false")) multiplexer_2 (
    .in0(dataIn[14]), .in1(dataIn[10]), .out(multiplexer_2_out), .sel(shft[2]));
  Multiplexer #(.enable("false")) multiplexer_3 (
    .in0(dataIn[13]), .in1(dataIn[9]), .out(multiplexer_3_out), .sel(shft[2]));
  Multiplexer #(.enable("false")) multiplexer_4 (
    .in0(dataIn[12]), .in1(dataIn[8]), .out(multiplexer_4_out), .sel(shft[2]));
  Multiplexer #(.enable("false")) multiplexer_5 (
    .in0(dataIn[11]), .in1(dataIn[7]), .out(multiplexer_5_out), .sel(shft[2]));
  Multiplexer #(.enable("false")) multiplexer_6 (
    .in0(dataIn[10]), .in1(dataIn[6]), .out(multiplexer_6_out), .sel(shft[2]));
  Multiplexer #(.enable("false")) multiplexer_7 (
    .in0(dataIn[9]), .in1(dataIn[5]), .out(multiplexer_7_out), .sel(shft[2]));
  Multiplexer #(.enable("false")) multiplexer_8 (
    .in0(dataIn[8]), .in1(dataIn[4]), .out(multiplexer_8_out), .sel(shft[2]));
  Multiplexer #(.enable("false")) multiplexer_9 (
    .in0(dataIn[7]), .in1(dataIn[3]), .out(multiplexer_9_out), .sel(shft[2]));
  Multiplexer #(.enable("false")) multiplexer_10 (
    .in0(dataIn[6]), .in1(dataIn[2]), .out(multiplexer_10_out), .sel(shft[2]));
  Multiplexer #(.enable("false")) multiplexer_11 (
    .in0(dataIn[5]), .in1(dataIn[1]), .out(multiplexer_11_out), .sel(shft[2]));
  Multiplexer #(.enable("false")) multiplexer_12 (
    .in0(dataIn[4]), .in1(dataIn[0]), .out(multiplexer_12_out), .sel(shft[2]));
  Multiplexer #(.enable("false")) multiplexer_13 (.in0(dataIn[3]), .in1(1'b0), .out(multiplexer_13_out), .sel(shft[2]));
  Multiplexer #(.enable("false")) multiplexer_14 (.in0(dataIn[2]), .in1(1'b0), .out(multiplexer_14_out), .sel(shft[2]));
  Multiplexer #(.enable("false")) multiplexer_15 (.in0(dataIn[1]), .in1(1'b0), .out(multiplexer_15_out), .sel(shft[2]));
  Multiplexer #(.enable("false")) multiplexer_16 (.in0(dataIn[0]), .in1(1'b0), .out(multiplexer_16_out), .sel(shft[2]));
  Multiplexer #(.enable("false")) multiplexer_17 (
    .in0(multiplexer_1_out), .in1(multiplexer_3_out), .out(multiplexer_17_out), .sel(shft[1]));
  Multiplexer #(.enable("false")) multiplexer_18 (
    .in0(multiplexer_2_out), .in1(multiplexer_4_out), .out(multiplexer_18_out), .sel(shft[1]));
  Multiplexer #(.enable("false")) multiplexer_19 (
    .in0(multiplexer_3_out), .in1(multiplexer_5_out), .out(multiplexer_19_out), .sel(shft[1]));
  Multiplexer #(.enable("false")) multiplexer_20 (
    .in0(multiplexer_4_out), .in1(multiplexer_6_out), .out(multiplexer_20_out), .sel(shft[1]));
  Multiplexer #(.enable("false")) multiplexer_21 (
    .in0(multiplexer_5_out), .in1(multiplexer_7_out), .out(multiplexer_21_out), .sel(shft[1]));
  Multiplexer #(.enable("false")) multiplexer_22 (
    .in0(multiplexer_6_out), .in1(multiplexer_8_out), .out(multiplexer_22_out), .sel(shft[1]));
  Multiplexer #(.enable("false")) multiplexer_23 (
    .in0(multiplexer_7_out), .in1(multiplexer_9_out), .out(multiplexer_23_out), .sel(shft[1]));
  Multiplexer #(.enable("false")) multiplexer_24 (
    .in0(multiplexer_8_out), .in1(multiplexer_10_out), .out(multiplexer_24_out), .sel(shft[1]));
  Multiplexer #(.enable("false")) multiplexer_25 (
    .in0(multiplexer_9_out), .in1(multiplexer_11_out), .out(multiplexer_25_out), .sel(shft[1]));
  Multiplexer #(.enable("false")) multiplexer_26 (
    .in0(multiplexer_10_out), .in1(multiplexer_12_out), .out(multiplexer_26_out), .sel(shft[1]));
  Multiplexer #(.enable("false")) multiplexer_27 (
    .in0(multiplexer_11_out), .in1(multiplexer_13_out), .out(multiplexer_27_out), .sel(shft[1]));
  Multiplexer #(.enable("false")) multiplexer_28 (
    .in0(multiplexer_12_out), .in1(multiplexer_14_out), .out(multiplexer_28_out), .sel(shft[1]));
  Multiplexer #(.enable("false")) multiplexer_29 (
    .in0(multiplexer_13_out), .in1(multiplexer_15_out), .out(multiplexer_29_out), .sel(shft[1]));
  Multiplexer #(.enable("false")) multiplexer_30 (
    .in0(multiplexer_14_out), .in1(multiplexer_16_out), .out(multiplexer_30_out), .sel(shft[1]));
  Multiplexer #(.enable("false")) multiplexer_31 (
    .in0(multiplexer_15_out), .in1(1'b0), .out(multiplexer_31_out), .sel(shft[1]));
  Multiplexer #(.enable("false")) multiplexer_32 (
    .in0(multiplexer_16_out), .in1(1'b0), .out(multiplexer_32_out), .sel(shft[1]));
  Multiplexer #(.enable("false")) multiplexer_33 (
    .in0(multiplexer_17_out), .in1(multiplexer_18_out), .out(dataOut[15]), .sel(shft[0]));
  Multiplexer #(.enable("false")) multiplexer_34 (
    .in0(multiplexer_18_out), .in1(multiplexer_19_out), .out(dataOut[14]), .sel(shft[0]));
  Multiplexer #(.enable("false")) multiplexer_35 (
    .in0(multiplexer_19_out), .in1(multiplexer_20_out), .out(dataOut[13]), .sel(shft[0]));
  Multiplexer #(.enable("false")) multiplexer_36 (
    .in0(multiplexer_20_out), .in1(multiplexer_21_out), .out(dataOut[12]), .sel(shft[0]));
  Multiplexer #(.enable("false")) multiplexer_37 (
    .in0(multiplexer_21_out), .in1(multiplexer_22_out), .out(dataOut[11]), .sel(shft[0]));
  Multiplexer #(.enable("false")) multiplexer_38 (
    .in0(multiplexer_22_out), .in1(multiplexer_23_out), .out(dataOut[10]), .sel(shft[0]));
  Multiplexer #(.enable("false")) multiplexer_39 (
    .in0(multiplexer_23_out), .in1(multiplexer_24_out), .out(dataOut[9]), .sel(shft[0]));
  Multiplexer #(.enable("false")) multiplexer_40 (
    .in0(multiplexer_24_out), .in1(multiplexer_25_out), .out(dataOut[8]), .sel(shft[0]));
  Multiplexer #(.enable("false")) multiplexer_41 (
    .in0(multiplexer_25_out), .in1(multiplexer_26_out), .out(dataOut[7]), .sel(shft[0]));
  Multiplexer #(.enable("false")) multiplexer_42 (
    .in0(multiplexer_26_out), .in1(multiplexer_27_out), .out(dataOut[6]), .sel(shft[0]));
  Multiplexer #(.enable("false")) multiplexer_43 (
    .in0(multiplexer_27_out), .in1(multiplexer_28_out), .out(dataOut[5]), .sel(shft[0]));
  Multiplexer #(.enable("false")) multiplexer_44 (
    .in0(multiplexer_28_out), .in1(multiplexer_29_out), .out(dataOut[4]), .sel(shft[0]));
  Multiplexer #(.enable("false")) multiplexer_45 (
    .in0(multiplexer_29_out), .in1(multiplexer_30_out), .out(dataOut[3]), .sel(shft[0]));
  Multiplexer #(.enable("false")) multiplexer_46 (
    .in0(multiplexer_30_out), .in1(multiplexer_31_out), .out(dataOut[2]), .sel(shft[0]));
  Multiplexer #(.enable("false")) multiplexer_47 (
    .in0(multiplexer_31_out), .in1(multiplexer_32_out), .out(dataOut[1]), .sel(shft[0]));
  Multiplexer #(.enable("false")) multiplexer_48 (
    .in0(multiplexer_32_out), .in1(1'b0), .out(dataOut[0]), .sel(shft[0]));

  // Other names for the same wires on the sheet: s0 = shft[0]; s1 = shft[1]; s2 = shft[2]
endmodule

module RShift (
  input  [15:0] shft,
  input  [15:0] dataIn,
  output [15:0] dataOut
);

  wire multiplexer_1_out, multiplexer_2_out, multiplexer_3_out, multiplexer_4_out, multiplexer_5_out,
       multiplexer_6_out, multiplexer_7_out, multiplexer_8_out, multiplexer_9_out, multiplexer_10_out,
       multiplexer_11_out, multiplexer_12_out, multiplexer_13_out, multiplexer_14_out, multiplexer_15_out,
       multiplexer_16_out, multiplexer_17_out, multiplexer_18_out, multiplexer_19_out, multiplexer_20_out,
       multiplexer_21_out, multiplexer_22_out, multiplexer_23_out, multiplexer_24_out, multiplexer_25_out,
       multiplexer_26_out, multiplexer_27_out, multiplexer_28_out, multiplexer_29_out, multiplexer_30_out,
       multiplexer_31_out, multiplexer_32_out;

  Multiplexer #(.enable("false")) multiplexer_1 (
    .in0(dataIn[0]), .in1(dataIn[4]), .out(multiplexer_1_out), .sel(shft[2]));
  Multiplexer #(.enable("false")) multiplexer_2 (
    .in0(dataIn[1]), .in1(dataIn[5]), .out(multiplexer_2_out), .sel(shft[2]));
  Multiplexer #(.enable("false")) multiplexer_3 (
    .in0(dataIn[2]), .in1(dataIn[6]), .out(multiplexer_3_out), .sel(shft[2]));
  Multiplexer #(.enable("false")) multiplexer_4 (
    .in0(dataIn[3]), .in1(dataIn[7]), .out(multiplexer_4_out), .sel(shft[2]));
  Multiplexer #(.enable("false")) multiplexer_5 (
    .in0(dataIn[4]), .in1(dataIn[8]), .out(multiplexer_5_out), .sel(shft[2]));
  Multiplexer #(.enable("false")) multiplexer_6 (
    .in0(dataIn[5]), .in1(dataIn[9]), .out(multiplexer_6_out), .sel(shft[2]));
  Multiplexer #(.enable("false")) multiplexer_7 (
    .in0(dataIn[6]), .in1(dataIn[10]), .out(multiplexer_7_out), .sel(shft[2]));
  Multiplexer #(.enable("false")) multiplexer_8 (
    .in0(dataIn[7]), .in1(dataIn[11]), .out(multiplexer_8_out), .sel(shft[2]));
  Multiplexer #(.enable("false")) multiplexer_9 (
    .in0(dataIn[8]), .in1(dataIn[12]), .out(multiplexer_9_out), .sel(shft[2]));
  Multiplexer #(.enable("false")) multiplexer_10 (
    .in0(dataIn[9]), .in1(dataIn[13]), .out(multiplexer_10_out), .sel(shft[2]));
  Multiplexer #(.enable("false")) multiplexer_11 (
    .in0(dataIn[10]), .in1(dataIn[14]), .out(multiplexer_11_out), .sel(shft[2]));
  Multiplexer #(.enable("false")) multiplexer_12 (
    .in0(dataIn[11]), .in1(dataIn[15]), .out(multiplexer_12_out), .sel(shft[2]));
  Multiplexer #(.enable("false")) multiplexer_13 (
    .in0(dataIn[12]), .in1(1'b0), .out(multiplexer_13_out), .sel(shft[2]));
  Multiplexer #(.enable("false")) multiplexer_14 (
    .in0(dataIn[13]), .in1(1'b0), .out(multiplexer_14_out), .sel(shft[2]));
  Multiplexer #(.enable("false")) multiplexer_15 (
    .in0(dataIn[14]), .in1(1'b0), .out(multiplexer_15_out), .sel(shft[2]));
  Multiplexer #(.enable("false")) multiplexer_16 (
    .in0(dataIn[15]), .in1(1'b0), .out(multiplexer_16_out), .sel(shft[2]));
  Multiplexer #(.enable("false")) multiplexer_17 (
    .in0(multiplexer_1_out), .in1(multiplexer_3_out), .out(multiplexer_17_out), .sel(shft[1]));
  Multiplexer #(.enable("false")) multiplexer_18 (
    .in0(multiplexer_2_out), .in1(multiplexer_4_out), .out(multiplexer_18_out), .sel(shft[1]));
  Multiplexer #(.enable("false")) multiplexer_19 (
    .in0(multiplexer_3_out), .in1(multiplexer_5_out), .out(multiplexer_19_out), .sel(shft[1]));
  Multiplexer #(.enable("false")) multiplexer_20 (
    .in0(multiplexer_4_out), .in1(multiplexer_6_out), .out(multiplexer_20_out), .sel(shft[1]));
  Multiplexer #(.enable("false")) multiplexer_21 (
    .in0(multiplexer_5_out), .in1(multiplexer_7_out), .out(multiplexer_21_out), .sel(shft[1]));
  Multiplexer #(.enable("false")) multiplexer_22 (
    .in0(multiplexer_6_out), .in1(multiplexer_8_out), .out(multiplexer_22_out), .sel(shft[1]));
  Multiplexer #(.enable("false")) multiplexer_23 (
    .in0(multiplexer_7_out), .in1(multiplexer_9_out), .out(multiplexer_23_out), .sel(shft[1]));
  Multiplexer #(.enable("false")) multiplexer_24 (
    .in0(multiplexer_8_out), .in1(multiplexer_10_out), .out(multiplexer_24_out), .sel(shft[1]));
  Multiplexer #(.enable("false")) multiplexer_25 (
    .in0(multiplexer_9_out), .in1(multiplexer_11_out), .out(multiplexer_25_out), .sel(shft[1]));
  Multiplexer #(.enable("false")) multiplexer_26 (
    .in0(multiplexer_10_out), .in1(multiplexer_12_out), .out(multiplexer_26_out), .sel(shft[1]));
  Multiplexer #(.enable("false")) multiplexer_27 (
    .in0(multiplexer_11_out), .in1(multiplexer_13_out), .out(multiplexer_27_out), .sel(shft[1]));
  Multiplexer #(.enable("false")) multiplexer_28 (
    .in0(multiplexer_12_out), .in1(multiplexer_14_out), .out(multiplexer_28_out), .sel(shft[1]));
  Multiplexer #(.enable("false")) multiplexer_29 (
    .in0(multiplexer_13_out), .in1(multiplexer_15_out), .out(multiplexer_29_out), .sel(shft[1]));
  Multiplexer #(.enable("false")) multiplexer_30 (
    .in0(multiplexer_14_out), .in1(multiplexer_16_out), .out(multiplexer_30_out), .sel(shft[1]));
  Multiplexer #(.enable("false")) multiplexer_31 (
    .in0(multiplexer_15_out), .in1(1'b0), .out(multiplexer_31_out), .sel(shft[1]));
  Multiplexer #(.enable("false")) multiplexer_32 (
    .in0(multiplexer_16_out), .in1(1'b0), .out(multiplexer_32_out), .sel(shft[1]));
  Multiplexer #(.enable("false")) multiplexer_33 (
    .in0(multiplexer_17_out), .in1(multiplexer_18_out), .out(dataOut[0]), .sel(shft[0]));
  Multiplexer #(.enable("false")) multiplexer_34 (
    .in0(multiplexer_18_out), .in1(multiplexer_19_out), .out(dataOut[1]), .sel(shft[0]));
  Multiplexer #(.enable("false")) multiplexer_35 (
    .in0(multiplexer_19_out), .in1(multiplexer_20_out), .out(dataOut[2]), .sel(shft[0]));
  Multiplexer #(.enable("false")) multiplexer_36 (
    .in0(multiplexer_20_out), .in1(multiplexer_21_out), .out(dataOut[3]), .sel(shft[0]));
  Multiplexer #(.enable("false")) multiplexer_37 (
    .in0(multiplexer_21_out), .in1(multiplexer_22_out), .out(dataOut[4]), .sel(shft[0]));
  Multiplexer #(.enable("false")) multiplexer_38 (
    .in0(multiplexer_22_out), .in1(multiplexer_23_out), .out(dataOut[5]), .sel(shft[0]));
  Multiplexer #(.enable("false")) multiplexer_39 (
    .in0(multiplexer_23_out), .in1(multiplexer_24_out), .out(dataOut[6]), .sel(shft[0]));
  Multiplexer #(.enable("false")) multiplexer_40 (
    .in0(multiplexer_24_out), .in1(multiplexer_25_out), .out(dataOut[7]), .sel(shft[0]));
  Multiplexer #(.enable("false")) multiplexer_41 (
    .in0(multiplexer_25_out), .in1(multiplexer_26_out), .out(dataOut[8]), .sel(shft[0]));
  Multiplexer #(.enable("false")) multiplexer_42 (
    .in0(multiplexer_26_out), .in1(multiplexer_27_out), .out(dataOut[9]), .sel(shft[0]));
  Multiplexer #(.enable("false")) multiplexer_43 (
    .in0(multiplexer_27_out), .in1(multiplexer_28_out), .out(dataOut[10]), .sel(shft[0]));
  Multiplexer #(.enable("false")) multiplexer_44 (
    .in0(multiplexer_28_out), .in1(multiplexer_29_out), .out(dataOut[11]), .sel(shft[0]));
  Multiplexer #(.enable("false")) multiplexer_45 (
    .in0(multiplexer_29_out), .in1(multiplexer_30_out), .out(dataOut[12]), .sel(shft[0]));
  Multiplexer #(.enable("false")) multiplexer_46 (
    .in0(multiplexer_30_out), .in1(multiplexer_31_out), .out(dataOut[13]), .sel(shft[0]));
  Multiplexer #(.enable("false")) multiplexer_47 (
    .in0(multiplexer_31_out), .in1(multiplexer_32_out), .out(dataOut[14]), .sel(shft[0]));
  Multiplexer #(.enable("false")) multiplexer_48 (
    .in0(multiplexer_32_out), .in1(1'b0), .out(dataOut[15]), .sel(shft[0]));

  // Other names for the same wires on the sheet: s0 = shft[0]; s1 = shft[1]; s2 = shft[2]
endmodule

module pc_reg (
  input  [15:0] dataIn,
  input  reset,
  input  clk,
  output [15:0] dataOut
);

  D_Flip_Flop #(.trigger("falling")) d_ff_1 (
    .D(dataIn[0]), .clk(clk), .Q(dataOut[0]), .reset(reset));  // open: Qn, preset
  D_Flip_Flop #(.trigger("falling")) d_ff_2 (
    .D(dataIn[1]), .clk(clk), .Q(dataOut[1]), .reset(reset));  // open: Qn, preset
  D_Flip_Flop #(.trigger("falling")) d_ff_3 (
    .D(dataIn[2]), .clk(clk), .Q(dataOut[2]), .reset(reset));  // open: Qn, preset
  D_Flip_Flop #(.trigger("falling")) d_ff_4 (
    .D(dataIn[3]), .clk(clk), .Q(dataOut[3]), .reset(reset));  // open: Qn, preset
  D_Flip_Flop #(.trigger("falling")) d_ff_5 (
    .D(dataIn[4]), .clk(clk), .Q(dataOut[4]), .reset(reset));  // open: Qn, preset
  D_Flip_Flop #(.trigger("falling")) d_ff_6 (
    .D(dataIn[5]), .clk(clk), .Q(dataOut[5]), .reset(reset));  // open: Qn, preset
  D_Flip_Flop #(.trigger("falling")) d_ff_7 (
    .D(dataIn[6]), .clk(clk), .Q(dataOut[6]), .reset(reset));  // open: Qn, preset
  D_Flip_Flop #(.trigger("falling")) d_ff_8 (
    .D(dataIn[7]), .clk(clk), .Q(dataOut[7]), .reset(reset));  // open: Qn, preset
  D_Flip_Flop #(.trigger("falling")) d_ff_9 (
    .D(dataIn[8]), .clk(clk), .Q(dataOut[8]), .reset(reset));  // open: Qn, preset
  D_Flip_Flop #(.trigger("falling")) d_ff_10 (
    .D(dataIn[9]), .clk(clk), .Q(dataOut[9]), .reset(reset));  // open: Qn, preset
  D_Flip_Flop #(.trigger("falling")) d_ff_11 (
    .D(dataIn[10]), .clk(clk), .Q(dataOut[10]), .reset(reset));  // open: Qn, preset
  D_Flip_Flop #(.trigger("falling")) d_ff_12 (
    .D(dataIn[11]), .clk(clk), .Q(dataOut[11]), .reset(reset));  // open: Qn, preset
  D_Flip_Flop #(.trigger("falling")) d_ff_13 (
    .D(dataIn[12]), .clk(clk), .Q(dataOut[12]), .reset(reset));  // open: Qn, preset
  D_Flip_Flop #(.trigger("falling")) d_ff_14 (
    .D(dataIn[13]), .clk(clk), .Q(dataOut[13]), .reset(reset));  // open: Qn, preset
  D_Flip_Flop #(.trigger("falling")) d_ff_15 (
    .D(dataIn[14]), .clk(clk), .Q(dataOut[14]), .reset(reset));  // open: Qn, preset
  D_Flip_Flop #(.trigger("falling")) d_ff_16 (
    .D(dataIn[15]), .clk(clk), .Q(dataOut[15]), .reset(reset));  // open: Qn, preset

  // Other names for the same wires on the sheet: in2[7:0] = dataIn[15:8]; out1[7:0] = dataOut[7:0]
endmodule

module control (
  input  [15:0] insn,
  output [2:0] rs,
  output [2:0] rt,
  output [2:0] rd,
  output [2:0] shamt,
  output [5:0] immed,
  output [11:0] addr,
  output Rwe,
  output DMwe,
  output Rdst,
  output Rwd,
  output [2:0] ALUop,
  output ALUinB,
  output beq,
  output bge,
  output j,
  output jr,
  output jal,
  output in_8060aaad,
  output out_b538a2af,
  output shft
);

  wire add, addi, nandd, norr, slll, srll, sub;

  Decoder #(.select(4)) decoder_1 (
    .out0(add), .out1(addi), .out2(sub), .out3(norr), .out4(nandd), .out5(slll), .out6(srll), .out7(Rwd),
    .out8(DMwe), .out9(beq), .out10(bge), .out11(j), .out12(jr), .out13(jal), .out14(in_8060aaad),
    .out15(out_b538a2af), .sel(insn[15:12]));  // open: en
  or or_1 (Rwe, add, addi, sub, norr, nandd, slll, srll, jal, Rwd, in_8060aaad);
  or or_2 (Rdst, Rwd, jal, addi, in_8060aaad);
  or or_3 (ALUinB, addi, slll, srll, Rwd, DMwe, jr, jal, in_8060aaad);
  or or_4 (shft, slll, srll);
  or or_5 (ALUop[1], norr, nandd);
  or or_6 (ALUop[2], slll, srll);
  or or_7 (ALUop[0], sub, nandd, srll, beq, bge);

  assign addr = insn[11:0];
  assign immed = insn[5:0];
  assign rd = insn[5:3];
  assign rs = insn[11:9];
  assign rt = insn[8:6];
  assign shamt = insn[2:0];

  // Other names for the same wires on the sheet: inn = in_8060aaad; opCode[3:0] = insn[15:12]; lw = Rwd;
  //   outt = out_b538a2af; sw = DMwe
endmodule

module extras (
  input  reset,
  input  [2:0] rd,
  input  [2:0] rt,
  input  [2:0] rs,
  input  [4:0] imm,
  input  [2:0] shamt,
  input  [11:0] address,
  input  RWE,
  input  DMWE,
  input  Jal,
  input  bge,
  input  inn,
  input  jr,
  input  j,
  input  shft
);

  wire clk;

  Clock u_clk (.out(clk));

  // Other names for the same wires on the sheet: addr[11:0] = address
endmodule
